// Logisim project BigASM.circ as structural Verilog
module BOARD_BIG_ASM (
  output out_1
);

  wire button_1_out, CLK, CLR, d_ff_1_q, not_1_out, Write, Write_ASCII;
  wire [6:0] ASCII;
  wire [7:0] counter_1_q;
  wire [23:0] Dir_INPUT, Dir_MEMORY;
  wire [31:0] INPUT, MEMORY_IN, MEMORY_OUT;

  Button button_1 (.out(button_1_out));
  Clock clock_1 (.out(CLK));
  D_Flip_Flop d_ff_1 (.clk(CLK), .D(1'b1), .Q(d_ff_1_q), .reset(button_1_out));  // open: Qn, preset, en
  D_Flip_Flop d_ff_2 (.clk(CLK), .D(d_ff_1_q), .Qn(CLR), .reset(button_1_out));  // open: Q, preset, en
  BIG_ASM big_asm_1 (
    .DATA_INPUT(INPUT), .MEMORY_IN(MEMORY_OUT), .CLK(CLK), .CLR(CLR), .DIR_INPUT(Dir_INPUT),
    .MEMORY_OUT(MEMORY_IN), .DIR_MEMORY(Dir_MEMORY), .Write_OUTPUT(Write), .ASCII(ASCII),
    .Write_ASCII(Write_ASCII), .END(out_1));
  MEMORY memory_1 (.DIR(Dir_MEMORY), .DATA_IN(MEMORY_IN), .WRITE(Write), .CLK(CLK), .CLR(CLR), .DATA_OUT(MEMORY_OUT));
  INPUT input_1 (.DIR(Dir_INPUT), .CLK(CLK), .DATA_OUT(INPUT));
  Counter counter_1 (.load(1'b0), .count(not_1_out), .Q(counter_1_q), .clk(CLK), .clr(CLR));  // open: D, carry
  not not_1 (not_1_out, out_1);
  // Probe on counter_1_q
  TTY #(.rows(32), .cols(60)) tty_1 (.data(ASCII), .clk(CLK), .we(Write_ASCII), .clr(CLR));

  // Other names for the same wires on the sheet: END = out_1

  // Notes on the sheet:
  //   COUNTER
  //   BOARD
endmodule

module INPUT (
  input  [23:0] DIR,
  input  CLK,
  output [31:0] DATA_OUT
);

  RAM #(.addrWidth(24), .dataWidth(32)) ram_1 (.addr(DIR), .data(DATA_OUT), .clk(CLK), .ld(1'b1));  // open: sel, clr
  // Probe on DATA_OUT
endmodule

module MEMORY (
  input  [23:0] DIR,
  input  [31:0] DATA_IN,
  input  WRITE,
  input  CLK,
  input  CLR,
  output [31:0] DATA_OUT
);

  wire not_1_out;

  not not_1 (not_1_out, WRITE);
  RAM #(.addrWidth(24), .dataWidth(32), .bus("separate")) ram_1 (
    .addr(DIR), .din(DATA_IN), .data(DATA_OUT), .str(WRITE), .clk(CLK), .ld(not_1_out), .clr(CLR));  // open: sel
endmodule

module BIG_ASM (
  input  [31:0] DATA_INPUT,
  input  [31:0] MEMORY_IN,
  input  CLK,
  input  CLR,
  output [23:0] DIR_INPUT,
  output [31:0] MEMORY_OUT,
  output [23:0] DIR_MEMORY,
  output Write_OUTPUT,
  output [6:0] ASCII,
  output Write_ASCII,
  output END
);

  wire c1, c2, control_unit_1_li, control_unit_1_lm, control_unit_1_out_8, control_unit_1_out_10,
       control_unit_1_out_12, control_unit_1_out_13, control_unit_1_out_14, start;

  CONTROL_UNIT control_unit_1 (
    .in_1(start), .in_2(CLR), .in_3(CLK), .in_4(c1), .in_5(c2), .write(Write_OUTPUT),
    .out_8(control_unit_1_out_8), .LI(control_unit_1_li), .out_10(control_unit_1_out_10),
    .LM(control_unit_1_lm), .out_12(control_unit_1_out_12), .out_13(control_unit_1_out_13),
    .out_14(control_unit_1_out_14), .\end (END));
  starter starter_1 (.in_1(CLR), .in_2(CLK), .start(start));
  Data_Path data_path_1 (
    .in_1(DATA_INPUT), .in_2(control_unit_1_out_8), .in_3(control_unit_1_li), .in_4(control_unit_1_out_10),
    .in_5(control_unit_1_lm), .in_6(control_unit_1_out_12), .in_7(control_unit_1_out_14),
    .in_8(control_unit_1_out_13), .in_9(CLK), .in_10(CLR), .hoja(c2), .I___N(c1), .INDEX(DIR_INPUT),
    .out_14(MEMORY_OUT), .out_15(DIR_MEMORY));

  // Other names for the same wires on the sheet: A_i[31:0] = DATA_INPUT; D_Out[31:0] = MEMORY_OUT;
  //   dir_I[23:0] = DIR_INPUT; m[23:0] = DIR_MEMORY; rst = CLR; w = Write_OUTPUT
endmodule

module PRINT_UDEC (
  input  [31:0] num,
  input  start,
  input  CLK,
  input  RST,
  output [6:0] ASCII,
  output Write_ASCII,
  output \end 
);

  wire _0_c, _0_n, demultiplexer_1_out0, demultiplexer_2_out0, demultiplexer_2_out1, demultiplexer_3_out0,
       demultiplexer_3_out1, IDLE_2_q, IDLE_3_q, IDLE_4_q, IDLE_q, Lc, Lc_0, Ln, Ln_0, or_1_out;
  wire [23:0] bit_extender_1_out;
  wire [31:0] c, c___1, c___1_t, divider_1_rem, memory_1_data_out, multiplexer_1_out, multiplexer_2_out,
       multiplexer_3_out, n, n___10, n___10___48;

  Multiplexer #(.width(32), .enable("false")) multiplexer_1 (
    .in0(num), .in1(n___10), .out(multiplexer_1_out), .sel(Lc_0));
  Divider #(.width(32)) divider_1 (.a(n), .b(32'ha), .out(n___10), .rem(divider_1_rem));  // open: upper
  Adder #(.width(32)) adder_1 (.a(divider_1_rem), .b(32'h30), .out(n___10___48));  // open: cin, cout
  or or_1 (or_1_out, demultiplexer_1_out0, \end );
  Register #(.width(32)) u_n (.D(multiplexer_1_out), .en(Ln), .Q(n), .clk(CLK), .clr(RST));
  D_Flip_Flop IDLE (.clk(CLK), .D(or_1_out), .Q(IDLE_q), .preset(RST));  // open: Qn, en, reset
  Demultiplexer #(.enable("false")) demultiplexer_1 (
    .out0(demultiplexer_1_out0), .out1(Ln_0), .in(IDLE_q), .sel(start));
  or or_2 (Write_ASCII, demultiplexer_3_out0, demultiplexer_2_out1);
  Multiplexer #(.width(32), .enable("false")) multiplexer_2 (
    .in0(c___1), .in1(c___1_t), .out(multiplexer_2_out), .sel(Write_ASCII));
  Adder #(.width(32)) adder_2 (.a(c), .b(32'h1), .out(c___1));  // open: cin, cout
  Subtractor #(.width(32)) subtractor_1 (.a(c), .b(32'h1), .out(c___1_t));  // open: bin, bout
  D_Flip_Flop IDLE_2 (.clk(CLK), .D(Ln_0), .Q(IDLE_2_q), .reset(RST));  // open: Qn, preset, en
  Register #(.width(32)) u_c (.D(multiplexer_2_out), .en(Lc), .Q(c), .clk(CLK), .clr(RST));
  or or_3 (Lc_0, IDLE_2_q, demultiplexer_3_out1);
  Multiplexer #(.width(32), .enable("false")) multiplexer_3 (
    .in0(c), .in1(c___1_t), .out(multiplexer_3_out), .sel(Write_ASCII));
  Comparator #(.width(32), .mode("unsigned")) comparator_1 (.a({32{1'b0}}), .b(n), .lt(_0_n));  // open: gt, eq
  Comparator #(.width(32), .mode("unsigned")) comparator_2 (.a({32{1'b0}}), .b(c), .lt(_0_c));  // open: gt, eq
  D_Flip_Flop IDLE_3 (.clk(CLK), .D(Write_ASCII), .Q(IDLE_3_q), .reset(RST));  // open: Qn, preset, en
  Demultiplexer #(.enable("false")) demultiplexer_2 (
    .out0(demultiplexer_2_out0), .out1(demultiplexer_2_out1), .in(IDLE_3_q), .sel(_0_c));
  Bit_Extender #(.in_width(32), .out_width(24)) bit_extender_1 (.in(multiplexer_3_out), .out(bit_extender_1_out));
  D_Flip_Flop IDLE_4 (.clk(CLK), .D(Lc_0), .Q(IDLE_4_q), .reset(RST));  // open: Qn, preset, en
  or or_4 (Lc, Lc_0, Write_ASCII);
  or or_5 (Ln, Ln_0, Lc_0);
  Demultiplexer #(.enable("false")) demultiplexer_3 (
    .out0(demultiplexer_3_out0), .out1(demultiplexer_3_out1), .in(IDLE_4_q), .sel(_0_n));
  D_Flip_Flop IDLE_5 (.clk(CLK), .D(demultiplexer_2_out0), .Q(\end ), .reset(RST));  // open: Qn, preset, en
  MEMORY memory_1 (
    .DIR(bit_extender_1_out), .DATA_IN(n___10___48), .WRITE(Lc_0), .CLK(CLK), .CLR(RST),
    .DATA_OUT(memory_1_data_out));
  Bit_Extender #(.in_width(32), .out_width(7)) bit_extender_2 (.in(memory_1_data_out), .out(ASCII));

  // Other names for the same wires on the sheet: Lc_1 = Write_ASCII; Sc = Write_ASCII; Ln_1 = Lc_0; Sn = Lc_0;
  //   Write = Lc_0
endmodule

module PRINT_DEC (
  input  [31:0] num,
  input  start,
  input  CLK,
  input  RST,
  output [6:0] ASCII,
  output Write_ASCII,
  output END
);

  wire demultiplexer_1_out0, demultiplexer_1_out1, demultiplexer_2_out0, demultiplexer_3_out0, end_t,
       IDLE_3_q, IDLE_q, or_1_out, or_2_out, or_3_out, S_ASCII, startUDEC, Write_ASCII_1;
  wire [6:0] ASCII_t;
  wire [31:0] multiplexer_1_out, negator_1_out;

  or or_1 (or_1_out, demultiplexer_1_out0, END);
  Negator #(.width(32)) negator_1 (.in(num), .out(negator_1_out));
  D_Flip_Flop IDLE (.clk(CLK), .D(or_1_out), .Q(IDLE_q), .preset(RST));  // open: Qn, en, reset
  Demultiplexer #(.enable("false")) demultiplexer_1 (
    .out0(demultiplexer_1_out0), .out1(demultiplexer_1_out1), .in(IDLE_q), .sel(start));
  Multiplexer #(.width(32), .enable("false")) multiplexer_1 (
    .in0(num), .in1(negator_1_out), .out(multiplexer_1_out), .sel(num[31]));
  Demultiplexer #(.enable("false")) demultiplexer_2 (
    .out0(demultiplexer_2_out0), .out1(S_ASCII), .in(demultiplexer_1_out1), .sel(num[31]));
  or or_2 (or_2_out, demultiplexer_2_out0, S_ASCII);
  D_Flip_Flop IDLE_2 (.clk(CLK), .D(or_2_out), .Q(startUDEC), .reset(RST));  // open: Qn, preset, en
  PRINT_UDEC print_udec_1 (
    .num(multiplexer_1_out), .start(startUDEC), .CLK(CLK), .RST(RST), .ASCII(ASCII_t),
    .Write_ASCII(Write_ASCII_1), .\end (end_t));
  D_Flip_Flop IDLE_3 (.clk(CLK), .D(or_3_out), .Q(IDLE_3_q), .reset(RST));  // open: Qn, preset, en
  or or_3 (or_3_out, startUDEC, demultiplexer_3_out0);
  Demultiplexer #(.enable("false")) demultiplexer_3 (
    .out0(demultiplexer_3_out0), .out1(END), .in(IDLE_3_q), .sel(end_t));
  Multiplexer #(.width(7), .enable("false")) multiplexer_2 (
    .in0(ASCII_t), .in1(7'b0101101), .out(ASCII), .sel(S_ASCII));
  or or_4 (Write_ASCII, S_ASCII, Write_ASCII_1);

  // Other names for the same wires on the sheet: sign = num[31]; Write_ASCII_0 = S_ASCII
endmodule

module TEST_PRINT (
  input  [31:0] in_1,
  output out_2
);

  wire button_1_out, button_2_out, CLK, CLR, d_ff_1_q, Write_ASCII;
  wire [6:0] ASCII;

  Button button_1 (.out(button_1_out));
  Clock clock_1 (.out(CLK));
  D_Flip_Flop d_ff_1 (.clk(CLK), .D(1'b1), .Q(d_ff_1_q), .reset(button_1_out));  // open: Qn, preset, en
  D_Flip_Flop d_ff_2 (.clk(CLK), .D(d_ff_1_q), .Qn(CLR), .reset(button_1_out));  // open: Q, preset, en
  Button button_2 (.out(button_2_out));
  PRINT_UDEC print_udec_1 ();  // open: num, start, CLK, RST, ASCII, Write_ASCII, end
  PRINT_DEC print_dec_1 (
    .num(in_1), .start(button_2_out), .CLK(CLK), .RST(CLR), .ASCII(ASCII), .Write_ASCII(Write_ASCII),
    .END(out_2));
  TTY #(.rows(32), .cols(60)) tty_1 (.data(ASCII), .clk(CLK), .we(Write_ASCII), .clr(CLR));
endmodule

module Data_Path (
  input  [31:0] in_1,
  input  in_2,
  input  in_3,
  input  in_4,
  input  in_5,
  input  in_6,
  input  in_7,
  input  in_8,
  input  in_9,
  input  in_10,
  output hoja,
  output I___N,
  output [23:0] INDEX,
  output [31:0] out_14,
  output [23:0] out_15
);

  wire _2I___1___N, _2I___2___N, HDer___0, HIzq___0, no_Hijo_Der, no_Hijo_Izq;
  wire [23:0] adder_1_out, bit_extender_1_out, M___1, multiplexer_4_out;
  wire [31:0] _2I___1, _2I___2, HDer, HIzq, I___1, multiplexer_1_out, multiplexer_3_out, multiplier_1_out, N;

  Multiplexer #(.width(32), .enable("false")) multiplexer_1 (
    .in0(_2I___1), .in1(_2I___2), .out(multiplexer_1_out), .sel(in_7));
  Bit_Extender #(.in_width(32), .out_width(24)) bit_extender_1 (.in(multiplexer_1_out), .out(bit_extender_1_out));
  Adder #(.width(24)) adder_1 (.a(24'h1), .b(bit_extender_1_out), .out(adder_1_out));  // open: cin, cout
  Multiplexer #(.width(24), .enable("false")) multiplexer_2 (
    .in0(adder_1_out), .in1({24{1'b0}}), .out(INDEX), .sel(in_2));
  Register #(.width(32)) R1 (.D(in_1), .en(in_2), .Q(N), .clk(in_9), .clr(in_10));
  Register #(.width(32)) R2 (.D(in_1), .en(in_8), .Q(HIzq), .clk(in_9), .clr(in_10));
  Register #(.width(32)) R3 (.D(in_1), .en(in_7), .Q(HDer), .clk(in_9), .clr(in_10));
  Multiplexer #(.width(32), .enable("false")) multiplexer_3 (
    .in0({32{1'b0}}), .in1(I___1), .out(multiplexer_3_out), .sel(in_4));
  Multiplexer #(.width(24), .enable("false")) multiplexer_4 (
    .in0({24{1'b0}}), .in1(M___1), .out(multiplexer_4_out), .sel(in_6));
  Register #(.width(32)) R4 (.D(multiplexer_3_out), .en(in_3), .Q(out_14), .clk(in_9), .clr(in_10));
  Register #(.width(24)) R5 (.D(multiplexer_4_out), .en(in_5), .Q(out_15), .clk(in_9), .clr(in_10));
  Adder #(.width(32)) adder_2 (.a(out_14), .b(32'h1), .out(I___1));  // open: cin, cout
  Adder #(.width(24)) adder_3 (.a(out_15), .b(24'h1), .out(M___1));  // open: cin, cout
  Multiplier #(.width(32)) multiplier_1 (.a(out_14), .b(32'h2), .out(multiplier_1_out));  // open: cin, cout
  Comparator #(.width(32), .mode("unsigned")) comparator_1 (.a(out_14), .b(N), .lt(I___N));  // open: gt, eq
  Comparator #(.width(32), .mode("unsigned")) comparator_2 (.a(_2I___1), .b(N), .gt(_2I___1___N));  // open: eq, lt
  Comparator #(.width(32), .mode("unsigned")) comparator_3 (.a(_2I___2), .b(N), .gt(_2I___2___N));  // open: eq, lt
  Adder #(.width(32)) adder_4 (.a(32'h1), .b(multiplier_1_out), .out(_2I___1));  // open: cin, cout
  Adder #(.width(32)) adder_5 (.a(multiplier_1_out), .b(32'h2), .out(_2I___2));  // open: cin, cout
  Comparator #(.width(32)) comparator_4 (.a(HIzq), .b({32{1'b0}}), .lt(HIzq___0));  // open: gt, eq
  Comparator #(.width(32)) comparator_5 (.a(HDer), .b({32{1'b0}}), .lt(HDer___0));  // open: gt, eq
  or or_1 (no_Hijo_Izq, _2I___1___N, HIzq___0);
  or or_2 (no_Hijo_Der, _2I___2___N, HDer___0);
  and and_1 (hoja, no_Hijo_Izq, no_Hijo_Der);

  // Other names for the same wires on the sheet: A_I[31:0] = in_1; clk = in_9; I[31:0] = out_14; LDer = in_7;
  //   LI = in_3; LIzq = in_8; LM = in_5; LN = in_2; M[23:0] = out_15; rst = in_10; SI = in_4; SM = in_6

  // Notes on the sheet:
  //   Control Signals
  //   INDEX
  //   DATA PATH
  //   RF
  //   ALU
endmodule

module CONTROL_UNIT (
  input  in_1,
  input  in_2,
  input  in_3,
  input  in_4,
  input  in_5,
  output \end ,
  output write,
  output out_8,
  output LI,
  output out_10,
  output LM,
  output out_12,
  output out_13,
  output out_14
);

  wire demultiplexer_1_out0, demultiplexer_2_out0, demultiplexer_3_out0, demultiplexer_3_out1,
       demultiplexer_4_out0, IDLE_q, or_1_out, or_4_out, or_5_out, or_6_out, WAIT_2_q, WHILE_q;

  or or_1 (or_1_out, demultiplexer_3_out1, demultiplexer_1_out0);
  D_Flip_Flop IDLE (.clk(in_3), .D(or_1_out), .Q(IDLE_q), .preset(1'b1));  // open: Qn, en, reset
  Demultiplexer #(.enable("false")) demultiplexer_1 (
    .out0(demultiplexer_1_out0), .out1(out_8), .in(IDLE_q), .sel(in_1));
  or or_2 (LI, out_8, out_10);
  or or_3 (LM, out_8, out_12);
  or or_4 (or_4_out, out_8, out_10);
  D_Flip_Flop WHILE (.clk(in_3), .D(or_4_out), .Q(WHILE_q), .reset(in_2));  // open: Qn, preset, en
  Demultiplexer #(.enable("false")) demultiplexer_2 (
    .out0(demultiplexer_2_out0), .out1(out_13), .in(WHILE_q), .sel(in_4));
  or or_5 (or_5_out, demultiplexer_3_out0, demultiplexer_2_out0);
  D_Flip_Flop u_END (.clk(in_3), .D(or_5_out), .Q(\end ), .reset(in_2));  // open: Qn, preset, en
  D_Flip_Flop WAIT (.clk(in_3), .D(out_13), .Q(out_14), .reset(in_2));  // open: Qn, preset, en
  Demultiplexer #(.enable("false")) demultiplexer_3 (
    .out0(demultiplexer_3_out0), .out1(demultiplexer_3_out1), .in(\end ), .sel(in_2));
  D_Flip_Flop AFTER_IF (.clk(in_3), .D(or_6_out), .Q(out_10), .reset(in_2));  // open: Qn, preset, en
  D_Flip_Flop WAIT_2 (.clk(in_3), .D(out_14), .Q(WAIT_2_q), .reset(in_2));  // open: Qn, preset, en
  Demultiplexer #(.enable("false")) demultiplexer_4 (
    .out0(demultiplexer_4_out0), .out1(write), .in(WAIT_2_q), .sel(in_5));
  or or_6 (or_6_out, demultiplexer_4_out0, out_12);
  D_Flip_Flop WAIT_3 (.clk(in_3), .D(write), .Q(out_12), .reset(in_2));  // open: Qn, preset, en

  // Other names for the same wires on the sheet: clk = in_3; Es_hoja = in_5; I___N = in_4; LDer = out_14;
  //   LIzq = out_13; LI0 = out_8; LM0 = out_8; LN = out_8; rst = in_2; LI1 = out_10; SI = out_10; LM1 = out_12;
  //   SM = out_12; start = in_1

  // Notes on the sheet:
  //   CONTROL UNIT
endmodule

module starter (
  input  in_1,
  input  in_2,
  output start
);

  wire en, not_1_out;

  D_Flip_Flop d_ff_1 (.clk(in_2), .D(1'b1), .Qn(en), .en(not_1_out), .reset(in_1));  // open: Q, preset
  not not_1 (not_1_out, in_1);
  and and_1 (start, ~in_1, en);  // AND_Gate

  // Other names for the same wires on the sheet: clk = in_2; rst = in_1

  // Notes on the sheet:
  //   Starter
endmodule
